// Logisim project ALU.circ as structural Verilog: 1 circuit, main circuit ALU
module ALU (
  input  [31:0] A,
  input  [31:0] B,
  input  [4:0] Shift,
  input  [3:0] Codop,
  input  CarryIn,
  output [31:0] S,
  output [3:0] Flags
);

  wire adder_1_cout, adder_2_cout, and_1_out, and_2_out, and_6_out, and_7_out, bitselector_1_out,
       bitselector_2_out, bitselector_3_out, bitselector_4_out, not_2_out, subtractor_1_bout,
       subtractor_2_bout, undriven, undriven_2, xor_2_out, xor_3_out, xor_4_out, xor_5_out;
  wire [31:0] adder_2_out, and_3_out, and_4_out, and_5_out, CMN, CMP, multiplier_1_out, negator_1_out,
       not_1_out, or_1_out, shifter_1_out, shifter_2_out, shifter_3_out, shifter_4_out, subtractor_2_out,
       xor_1_out;

  and and_1 (and_1_out, Codop[2], CarryIn);
  and and_2 (and_2_out, Codop[2], ~CarryIn);  // AND_Gate
  assign and_3_out = A & B;  // AND_Gate and_3, 32 bits wide
  assign xor_1_out = A ^ B;  // XOR_Gate xor_1, 32 bits wide
  Shifter #(.width(32)) shifter_1 (.in(B), .\dist (Shift), .out(shifter_1_out));
  Shifter #(.shift("lr"), .width(32)) shifter_2 (.in(B), .\dist (Shift), .out(shifter_2_out));
  Shifter #(.shift("ar"), .width(32)) shifter_3 (.in(B), .\dist (Shift), .out(shifter_3_out));
  Adder #(.width(32)) adder_1 (.a(A), .b(B), .out(CMP), .cin(and_1_out), .cout(adder_1_cout));
  Subtractor #(.width(32)) subtractor_1 (.a(B), .b(A), .out(CMN), .bin(and_2_out), .bout(subtractor_1_bout));
  Shifter #(.shift("rr"), .width(32)) shifter_4 (.in(B), .\dist (Shift), .out(shifter_4_out));
  assign and_4_out = A & B;  // AND_Gate and_4, 32 bits wide
  Negator #(.width(32)) negator_1 (.in(A), .out(negator_1_out));
  Subtractor #(.width(32)) subtractor_2 (.a(B), .b(A), .out(subtractor_2_out), .bin(1'b0), .bout(subtractor_2_bout));
  Adder #(.width(32)) adder_2 (.a(A), .b(B), .out(adder_2_out), .cin(1'b0), .cout(adder_2_cout));
  assign or_1_out = A | B;  // OR_Gate or_1, 32 bits wide
  Multiplier #(.width(32)) multiplier_1 (.a(A), .b(B), .out(multiplier_1_out), .cin({32{1'b0}}));  // open: cout
  assign and_5_out = B & ~A;  // AND_Gate and_5, 32 bits wide
  assign not_1_out = ~B;  // NOT_Gate not_1, 32 bits wide
  not not_2 (not_2_out, subtractor_1_bout);
  Multiplexer #(.enable("false"), .select(4), .width(32)) multiplexer_1 (
    .in0(and_3_out), .in1(xor_1_out), .in2(shifter_1_out), .in3(shifter_2_out), .in4(shifter_3_out),
    .in5(CMP), .in6(CMN), .in7(shifter_4_out), .in8(and_4_out), .in9(negator_1_out), .in10(subtractor_2_out),
    .in11(adder_2_out), .in12(or_1_out), .in13(multiplier_1_out), .in14(and_5_out), .in15(not_1_out),
    .out(S), .sel(Codop));
  Multiplexer #(.enable("false"), .select(4)) multiplexer_2 (
    .in0(1'b0), .in1(1'b0), .in2(1'b0), .in3(1'b0), .in4(1'b0), .in5(adder_1_cout), .in6(not_2_out),
    .in7(1'b0), .in8(1'b0), .in9(1'b0), .in10(subtractor_2_bout), .in11(adder_2_cout), .in12(1'b0),
    .in13(1'b0), .in14(1'b0), .in15(1'b0), .out(Flags[1]), .sel(Codop));
  BitSelector #(.width(32)) bitselector_1 (.in(CMP), .out(bitselector_1_out), .sel({5{1'b1}}));
  BitSelector #(.width(32)) bitselector_2 (.in(CMN), .out(bitselector_2_out), .sel({5{1'b1}}));
  Comparator #(.width(32)) comparator_1 (.a(S), .b({32{1'b0}}), .eq(Flags[2]), .lt(Flags[3]));  // open: gt
  BitSelector #(.width(32)) bitselector_3 (.in(A), .out(bitselector_3_out), .sel({5{1'b1}}));
  BitSelector #(.width(32)) bitselector_4 (.in(B), .out(bitselector_4_out), .sel({5{1'b1}}));
  xor xor_2 (xor_2_out, bitselector_4_out, bitselector_1_out);
  xor xor_3 (xor_3_out, bitselector_1_out, bitselector_3_out);
  xor xor_4 (xor_4_out, bitselector_4_out, bitselector_2_out);
  xor xor_5 (xor_5_out, bitselector_2_out, bitselector_3_out);
  and and_6 (and_6_out, xor_2_out, xor_3_out);
  and and_7 (and_7_out, xor_4_out, xor_5_out);
  Multiplexer #(.enable("false"), .select(4)) multiplexer_3 (
    .in0(1'b0), .in1(1'b0), .in2(1'b0), .in3(1'b0), .in4(1'b0), .in5(and_6_out), .in6(and_7_out), .in7(1'b0),
    .in8(1'b0), .in9(1'b0), .in10(undriven), .in11(undriven_2), .in12(1'b0), .in13(1'b0), .in14(1'b0),
    .in15(1'b0), .out(Flags[0]), .sel(Codop));

  // Other names for the same wires on the sheet: V = Flags[0]; C = Flags[1]; Z = Flags[2]; N = Flags[3]

  // Notes on the sheet:
  //   Note: for ROR, C = N
  //   Note 2: assume that shift > 0 for LSL and LSR
endmodule
