// Logisim project Ctl_Data_Processing.circ as structural Verilog: 2 circuits, main circuit Data_Processing
module Data_Processing (
  input  Enable,
  input  [15:0] Instruction,
  output [2:0] Rd,
  output [2:0] Rn,
  output [2:0] Rm,
  output [3:0] ALU_Opcode,
  output [3:0] Flags_Update_Mask
);

  Multiplexer #(.enable("false"), .width(4)) multiplexer_1 (
    .in0(4'b0000), .in1(Instruction[9:6]), .out(ALU_Opcode), .sel(Enable));

  // Other names for the same wires on the sheet: en = Enable; b0 = Instruction[0]; b1 = Instruction[1];
  //   b2 = Instruction[2]; b3 = Instruction[3]; b4 = Instruction[4]; b5 = Instruction[5]; b10 = Instruction[10];
  //   b11 = Instruction[11]; b12 = Instruction[12]; b13 = Instruction[13]; b14 = Instruction[14];
  //   b15 = Instruction[15]; b6 = Instruction[6]; opcode[3:0] = Instruction[9:6]; b7 = Instruction[7];
  //   b8 = Instruction[8]; b9 = Instruction[9]

  // Notes on the sheet:
  //   Pull output low on Enable = 0
  //   Note 2: RSB instruction has Rn as 1st operand.
  //   MUL instruction has Rn as 1st operand and Rdm as 2nd operand
  //   For simplification purposes, Rm is used for 1st operand both here and in the ALU.
  //   Note: instructions that does not save the result will still have the second operand as the destination register, the ALU will copy the second register to the destination register
endmodule

module flags (
  input  [3:0] opcode,
  output [3:0] flag
);

  wire and_1_out, and_2_out, and_3_out, and_4_out, and_5_out, and_6_out, and_7_out, and_8_out, and_9_out,
       and_10_out, and_11_out, and_12_out, and_13_out, and_14_out, and_15_out, not_1_out, not_2_out,
       not_3_out, not_4_out, not_5_out, not_6_out, not_7_out, not_8_out, not_9_out, not_10_out, not_11_out,
       not_12_out, not_13_out, not_14_out, not_15_out, not_16_out, not_17_out, not_18_out, not_19_out,
       not_20_out, not_21_out, not_22_out, not_23_out, not_24_out, not_25_out, not_26_out, not_27_out,
       not_28_out, not_29_out, not_30_out, not_31_out, not_32_out, not_33_out, not_34_out, not_35_out,
       or_1_out, or_3_out;
  wire [3:0] multiplexer_1_out, multiplexer_2_out;

  not not_1 (not_1_out, opcode[0]);
  not not_2 (not_2_out, opcode[1]);
  not not_3 (not_3_out, opcode[2]);
  not not_4 (not_4_out, opcode[3]);
  not not_5 (not_5_out, opcode[1]);
  not not_6 (not_6_out, opcode[2]);
  not not_7 (not_7_out, opcode[3]);
  not not_8 (not_8_out, opcode[0]);
  not not_9 (not_9_out, opcode[2]);
  not not_10 (not_10_out, opcode[3]);
  not not_11 (not_11_out, opcode[2]);
  not not_12 (not_12_out, opcode[3]);
  not not_13 (not_13_out, opcode[0]);
  not not_14 (not_14_out, opcode[1]);
  not not_15 (not_15_out, opcode[3]);
  not not_16 (not_16_out, opcode[3]);
  not not_17 (not_17_out, opcode[0]);
  not not_18 (not_18_out, opcode[1]);
  not not_19 (not_19_out, opcode[2]);
  not not_20 (not_20_out, opcode[0]);
  not not_21 (not_21_out, opcode[1]);
  not not_22 (not_22_out, opcode[0]);
  and and_1 (and_1_out, not_1_out, not_2_out, not_3_out, not_4_out);
  and and_2 (and_2_out, opcode[0], not_5_out, not_6_out, not_7_out);
  and and_3 (and_3_out, not_8_out, opcode[1], not_9_out, not_10_out);
  and and_4 (and_4_out, opcode[0], opcode[1], not_11_out, not_12_out);
  and and_5 (and_5_out, not_13_out, not_14_out, opcode[2], not_15_out);
  and and_6 (and_6_out, opcode[0], opcode[1], opcode[2], not_16_out);
  and and_7 (and_7_out, not_17_out, not_18_out, not_19_out, opcode[3]);
  and and_8 (and_8_out, not_20_out, not_21_out, opcode[2], opcode[3]);
  and and_9 (and_9_out, not_22_out, opcode[1], opcode[2], opcode[3]);
  and and_10 (and_10_out, opcode[0], opcode[1], opcode[2], opcode[3]);
  or or_1 (or_1_out, and_1_out, and_2_out, and_3_out, and_4_out, and_5_out, and_6_out, and_7_out, and_8_out, and_9_out, and_10_out);
  Multiplexer #(.enable("false"), .width(4)) multiplexer_1 (
    .in0(4'b0000), .in1(4'b1110), .out(multiplexer_1_out), .sel(or_1_out));
  // OR_Gate or_2 has open pins: out=flag
  not not_23 (not_23_out, opcode[1]);
  not not_24 (not_24_out, opcode[3]);
  not not_25 (not_25_out, opcode[0]);
  not not_26 (not_26_out, opcode[3]);
  not not_27 (not_27_out, opcode[1]);
  not not_28 (not_28_out, opcode[2]);
  not not_29 (not_29_out, opcode[0]);
  not not_30 (not_30_out, opcode[2]);
  not not_31 (not_31_out, opcode[2]);
  and and_11 (and_11_out, opcode[0], not_23_out, opcode[2], not_24_out);
  and and_12 (and_12_out, not_25_out, opcode[1], opcode[2], not_26_out);
  and and_13 (and_13_out, opcode[0], not_27_out, not_28_out, opcode[3]);
  and and_14 (and_14_out, not_29_out, opcode[1], not_30_out, opcode[3]);
  and and_15 (and_15_out, opcode[0], opcode[1], not_31_out, opcode[3]);
  or or_3 (or_3_out, and_11_out, and_12_out, and_13_out, and_14_out, and_15_out);
  Multiplexer #(.enable("false"), .width(4)) multiplexer_2 (
    .in0(4'b0000), .in1(4'b1110), .out(multiplexer_2_out), .sel(or_3_out));
  not not_32 (not_32_out, opcode[0]);
  not not_33 (not_33_out, opcode[1]);
  not not_34 (not_34_out, opcode[2]);
  not not_35 (not_35_out, opcode[3]);
  // AND_Gate and_16 has open pins: in0=not_32_out, in1=not_33_out, in2=not_34_out, in3=not_35_out, out=open

  // Other names for the same wires on the sheet: b6 = opcode[0]; b7 = opcode[1]; b8 = opcode[2]; b9 = opcode[3]
endmodule
