// Logisim project Ctl_Shift_Add_Sub_Mov.circ as structural Verilog: 3 circuits, main circuit Shift_Add_Sub_Mov
module Shift_Add_Sub_Mov (
  input  Enable,
  input  [15:0] Instruction,
  output Carry,
  output Imm32_Enable,
  output [2:0] Rm,
  output [2:0] Rn,
  output [2:0] Rd,
  output [4:0] Imm5,
  output [31:0] Imm32,
  output [3:0] ALU_Opcode,
  output [3:0] Flags_Update_Mask
);

  wire ADD, ADD3, ADD8, add_sub_r_i, ASR, b0, b1, b2, b3, b4, b5, b6, b7, b8, b9, b10, b11, b12, b13, b14,
       b15, CMP, decal, en_autre, en_imm3, en_imm5, en_imm8, en_imm32, LSL, LSR, MOV, not_1_out, not_2_out,
       not_3_out, not_4_out, not_5_out, not_6_out, not_7_out, not_8_out, not_9_out, not_10_out, not_11_out,
       not_12_out, not_13_out, not_14_out, not_15_out, not_16_out, not_17_out, not_18_out, not_19_out,
       or_1_out, or_8_out, or_10_out, SUB, SUB3, SUB8;
  wire [2:0] bit_extender_2_out, bit_extender_5_out, bit_extender_6_out, bit_extender_7_out, imm3,
       multiplexer_13_out, rd1, rd2, rd3, rd4, rm1, rm2, rn1, rn2, rn3;
  wire [3:0] flag, res;
  wire [4:0] imm5_t;
  wire [7:0] imm8;
  wire [15:0] bit_extender_1_out;
  wire [31:0] bit_extender_3_out, bit_extender_4_out, imm32_t, multiplexer_3_out, negator_1_out;

  or or_1 (or_1_out, LSL, LSR, ASR);
  assign bit_extender_1_out = {{15{Enable}}, Enable};  // Bit_Extender bit_extender_1
  assign bit_extender_2_out = {{2{or_1_out}}, or_1_out};  // Bit_Extender bit_extender_2
  Multiplexer #(.width(5)) multiplexer_1 (.in0({5{1'b0}}), .in1({b10, b9, b8, b7, b6}), .out(imm5_t), .sel(en_imm5));
  assign bit_extender_3_out = {{29{1'b0}}, imm3};  // Bit_Extender bit_extender_3
  assign bit_extender_4_out = {{24{1'b0}}, imm8};  // Bit_Extender bit_extender_4
  assign {b15, b14, b13, b12, b11, b10, b9, b8, b7, b6, b5, b4, b3, b2, b1, b0} = Instruction & bit_extender_1_out;  // AND_Gate and_1, 16 bits wide
  assign rd1 = bit_extender_2_out & {b2, b1, b0};  // AND_Gate and_2, 3 bits wide
  Multiplexer #(.width(3)) multiplexer_2 (.in0(3'b000), .in1({b5, b4, b3}), .out(rm1), .sel(en_imm5));
  Negator #(.width(32)) negator_1 (.in(bit_extender_4_out), .out(negator_1_out));
  Multiplexer #(.width(32)) multiplexer_3 (
    .in0(bit_extender_4_out), .in1(negator_1_out), .out(multiplexer_3_out), .sel(MOV));
  assign imm32_t = bit_extender_3_out | multiplexer_3_out;  // OR_Gate or_2, 32 bits wide
  opcode opcode_1 (
    .ADD(ADD), .ADD3(ADD3), .ADD8(ADD8), .SUB(SUB), .SUB3(SUB3), .SUB8(SUB8), .LSL(LSL), .LSR(LSR),
    .ASR(ASR), .MOV(MOV), .CMP(CMP), .res(res));
  not not_1 (not_1_out, b11);
  not not_2 (not_2_out, b12);
  not not_3 (not_3_out, b13);
  not not_4 (not_4_out, b12);
  not not_5 (not_5_out, b13);
  not not_6 (not_6_out, b11);
  not not_7 (not_7_out, b13);
  not not_8 (not_8_out, b9);
  not not_9 (not_9_out, b10);
  not not_10 (not_10_out, b13);
  Multiplexer multiplexer_4 (.in0(1'b0), .in1(b9), .out(add_sub_r_i), .sel(en_autre));
  assign bit_extender_5_out = {{2{add_sub_r_i}}, add_sub_r_i};  // Bit_Extender bit_extender_5
  Multiplexer #(.width(3)) multiplexer_5 (.in0(bit_extender_5_out), .in1({b2, b1, b0}), .out(rd2), .sel(en_autre));
  assign bit_extender_6_out = {{2{add_sub_r_i}}, add_sub_r_i};  // Bit_Extender bit_extender_6
  Multiplexer #(.width(3)) multiplexer_6 (.in0(bit_extender_6_out), .in1({b5, b4, b3}), .out(rn1), .sel(en_autre));
  assign bit_extender_7_out = {{2{add_sub_r_i}}, add_sub_r_i};  // Bit_Extender bit_extender_7
  Multiplexer #(.width(3)) multiplexer_7 (.in0(bit_extender_7_out), .in1({b8, b7, b6}), .out(rm2), .sel(en_autre));
  and and_3 (LSL, not_1_out, not_2_out, not_3_out);
  and and_4 (LSR, b11, not_4_out, not_5_out);
  and and_5 (ASR, not_6_out, b12, not_7_out);
  and and_6 (ADD, not_8_out, not_9_out, b11, b12, not_10_out);
  not not_11 (not_11_out, b10);
  not not_12 (not_12_out, b13);
  not not_13 (not_13_out, b9);
  not not_14 (not_14_out, b13);
  not not_15 (not_15_out, b13);
  Multiplexer #(.width(3)) multiplexer_8 (.in0(3'b000), .in1({b2, b1, b0}), .out(rd3), .sel(en_imm3));
  Multiplexer #(.width(3)) multiplexer_9 (.in0(3'b000), .in1({b5, b4, b3}), .out(rn2), .sel(en_imm3));
  Multiplexer #(.width(3)) multiplexer_10 (.in0(3'b000), .in1({b8, b7, b6}), .out(imm3), .sel(en_imm3));
  and and_7 (SUB, b9, not_11_out, b11, b12, not_12_out);
  and and_8 (ADD3, not_13_out, b10, b11, b12, not_14_out);
  and and_9 (SUB3, b9, b10, b11, b12, not_15_out);
  or or_3 (en_imm32, en_imm3, en_imm8);
  flags flags_1 (
    .ADD(ADD), .ADD3(ADD3), .ADD8(ADD8), .SUB(SUB), .SUB3(SUB3), .SUB8(SUB8), .LSL(LSL), .LSR(LSR),
    .ASR(ASR), .MOV(MOV), .CMP(CMP), .flag(flag));
  not not_16 (not_16_out, b11);
  not not_17 (not_17_out, b12);
  not not_18 (not_18_out, b12);
  not not_19 (not_19_out, b11);
  Multiplexer #(.width(3)) multiplexer_11 (.in0(3'b000), .in1({b10, b9, b8}), .out(rd4), .sel(en_imm8));
  Multiplexer #(.width(8)) multiplexer_12 (
    .in0({8{1'b0}}), .in1({b7, b6, b5, b4, b3, b2, b1, b0}), .out(imm8), .sel(en_imm8));
  and and_10 (MOV, not_16_out, not_17_out, b13);
  and and_11 (CMP, b11, not_18_out, b13);
  and and_12 (ADD8, not_19_out, b12, b13);
  and and_13 (SUB8, b11, b12, b13);
  or or_4 (en_imm5, LSL, LSR, ASR);
  or or_5 (en_autre, ADD, SUB);
  or or_6 (en_imm3, ADD3, SUB3);
  or or_7 (en_imm8, MOV, CMP, ADD8, SUB8);
  or or_8 (or_8_out, MOV, CMP);
  assign rn3 = rm1 | rd4;  // OR_Gate or_9, 3 bits wide
  not not_20 (decal, or_8_out);
  or or_10 (or_10_out, SUB, SUB3, SUB8);
  Multiplexer #(.width(3)) multiplexer_13 (.in0(3'b000), .in1(rn3), .out(multiplexer_13_out), .sel(decal));
  and and_14 (Carry, or_10_out, Enable);
  and and_15 (Imm32_Enable, en_imm32, Enable);
  assign Rm = rm1 | rm2;  // OR_Gate or_11, 3 bits wide
  assign Rn = rn1 | rn2 | multiplexer_13_out;  // OR_Gate or_12, 3 bits wide
  assign Rd = rd1 | rd2 | rd3 | rd4;  // OR_Gate or_13, 3 bits wide
  Multiplexer #(.width(5)) multiplexer_14 (.in0({5{1'b0}}), .in1(imm5_t), .out(Imm5), .sel(Enable));
  Multiplexer #(.width(32)) multiplexer_15 (.in0({32{1'b0}}), .in1(imm32_t), .out(Imm32), .sel(Enable));
  Multiplexer #(.width(4)) multiplexer_16 (.in0(4'b0000), .in1(res), .out(ALU_Opcode), .sel(Enable));
  Multiplexer #(.width(4)) multiplexer_17 (.in0(4'b0000), .in1(flag), .out(Flags_Update_Mask), .sel(Enable));

  // Other names for the same wires on the sheet: en = Enable

  // Notes on the sheet:
  //   Pull output low on Enable = 0
  //   Note 3: Imm32_Enable forces the use of the immediate for Rm register
  //   Note: ALU uses Rn register for shifts. Use Rn instead of Rm for shifts (immediate) here too
  //   Note 2: MOV uses RSB ALU opcode with Imm8 reversed so that it is copied to output register
  //   Enable carry for SUB since it is reversed in ALU
  //   only ADD and SUB use Rm
  //   ALU will use Imm32 instead of Rm
endmodule

module opcode (
  input  ADD,
  input  ADD3,
  input  ADD8,
  input  SUB,
  input  SUB3,
  input  SUB8,
  input  LSL,
  input  LSR,
  input  ASR,
  input  MOV,
  input  CMP,
  output [3:0] res
);

  wire GADD, GSUB;
  wire [3:0] res_ASR, res_CMP, res_GADD, res_GSUB, res_LSL, res_LSR, res_MOV;

  assign res = res_LSL | res_LSR | res_GADD | res_GSUB | res_ASR | res_MOV | res_CMP;  // OR_Gate or_1, 4 bits wide
  or or_2 (GADD, ADD, ADD3, ADD8);
  or or_3 (GSUB, SUB, SUB3, SUB8);
  Multiplexer #(.width(4)) multiplexer_1 (.in0(4'b0000), .in1(4'b0010), .out(res_LSL), .sel(LSL));
  Multiplexer #(.width(4)) multiplexer_2 (.in0(4'b0000), .in1(4'b0011), .out(res_LSR), .sel(LSR));
  Multiplexer #(.width(4)) multiplexer_3 (.in0(4'b0000), .in1(4'b0101), .out(res_GADD), .sel(GADD));
  Multiplexer #(.width(4)) multiplexer_4 (.in0(4'b0000), .in1(4'b0110), .out(res_GSUB), .sel(GSUB));
  Multiplexer #(.width(4)) multiplexer_5 (.in0(4'b0000), .in1(4'b0100), .out(res_ASR), .sel(ASR));
  Multiplexer #(.width(4)) multiplexer_6 (.in0(4'b0000), .in1(4'b1001), .out(res_MOV), .sel(MOV));
  Multiplexer #(.width(4)) multiplexer_7 (.in0(4'b0000), .in1(4'b1010), .out(res_CMP), .sel(CMP));
endmodule

module flags (
  input  ADD,
  input  ADD3,
  input  ADD8,
  input  SUB,
  input  SUB3,
  input  SUB8,
  input  LSL,
  input  LSR,
  input  ASR,
  input  MOV,
  input  CMP,
  output [3:0] flag
);

  wire GADD, GSUB;
  wire [3:0] res_ASR, res_CMP, res_GADD, res_GSUB, res_LSL, res_LSR, res_MOV;

  assign flag = res_LSL | res_LSR | res_GADD | res_GSUB | res_ASR | res_MOV | res_CMP;  // OR_Gate or_1, 4 bits wide
  or or_2 (GADD, ADD, ADD3, ADD8);
  or or_3 (GSUB, SUB, SUB3, SUB8);
  Multiplexer #(.width(4)) multiplexer_1 (.in0(4'b0000), .in1(4'b1110), .out(res_LSL), .sel(LSL));
  Multiplexer #(.width(4)) multiplexer_2 (.in0(4'b0000), .in1(4'b1110), .out(res_LSR), .sel(LSR));
  Multiplexer #(.width(4)) multiplexer_3 (.in0(4'b0000), .in1(4'b1111), .out(res_GADD), .sel(GADD));
  Multiplexer #(.width(4)) multiplexer_4 (.in0(4'b0000), .in1(4'b1111), .out(res_GSUB), .sel(GSUB));
  Multiplexer #(.width(4)) multiplexer_5 (.in0(4'b0000), .in1(4'b1110), .out(res_ASR), .sel(ASR));
  Multiplexer #(.width(4)) multiplexer_6 (.in0(4'b0000), .in1(4'b1100), .out(res_MOV), .sel(MOV));
  Multiplexer #(.width(4)) multiplexer_7 (.in0(4'b0000), .in1(4'b1111), .out(res_CMP), .sel(CMP));
endmodule
